// Logisim project cpu.circ as structural Verilog: 10 circuits, main circuit cpu
module cpu (
);

  wire CLK, controller_1_out_5, controller_1_out_7, controller_1_out_10, controller_1_out_11,
       controller_1_out_12, controller_1_out_15, controller_1_out_16, controller_1_out_19,
       controller_1_out_20, controller_1_out_21, Go, IR1, IR2, IR3, npc_1_out_11, RST, W1, W2, W3;
  wire [1:0] controller_1_out_13, controller_1_out_17;
  wire [2:0] controller_1_out_8;
  wire [3:0] controller_1_out_6, controller_1_out_14;
  wire [4:0] decoder_1_out_2, decoder_1_out_4, decoder_1_out_6, decoder_1_out_8, multiplexer_2_out,
       multiplexer_3_out, registerfile_1_p6;
  wire [5:0] decoder_1_out_3, decoder_1_out_7;
  wire [9:0] divider_1_out_2;
  wire [15:0] decoder_1_out_9, \总周期数 , \无条件分支指令数 , \有条件分支成功跳转 , \有条件分支指令数 ;
  wire [23:0] divider1_1_out_2;
  wire [25:0] decoder_1_out_5;
  wire [31:0] alu_1_result, extender_1_out_3, extender_1_out_4, interrupt_1_pc_out, mips_ram_1_p8,
       multiplexer_1_out, multiplexer_5_out, multiplexer_6_out, npc_1_out_10, npc_1_out_12, PC_q,
       registerfile_1_p7, registerfile_1_p8, rom_1_data, SyscallOut;

  Register #(.width(32)) PC (.D(interrupt_1_pc_out), .en(npc_1_out_11), .Q(PC_q), .clk(CLK), .clr(RST));
  interrupt interrupt_1 (
    .intr_btn1(IR1), .intr_LED1(W1), .PC_out(interrupt_1_pc_out), .intr_btn2(IR2), .intr_LED2(W2),
    .intr_btn3(IR3), .intr_LED3(W3), .eret(controller_1_out_19), .PC(npc_1_out_10));
  SumPeriod sumperiod_1 (.in_1(npc_1_out_11), .in_2(CLK), .out_4(\总周期数 ), .in_3(RST));
  Button \u_总复位  (.out(RST));
  Button _1 (.out(IR1));
  Button _2 (.out(IR2));
  Button _3 (.out(IR3));
  Clock clock_1 (.out(CLK));
  Button \u_继续运行  (.out(Go));
  LED led_1 (.in(W1));
  LED led_2 (.in(W2));
  LED led_3 (.in(W3));
  NPC npc_1 (
    .in_2(PC_q), .out_10(npc_1_out_10), .in_8(decoder_1_out_5), .in_1(decoder_1_out_9),
    .in_4(registerfile_1_p7), .in_5(controller_1_out_8), .out_12(npc_1_out_12), .in_9(registerfile_1_p8),
    .in_7(RST), .in_6(CLK), .out_13(\有条件分支成功跳转 ), .in_3(controller_1_out_21), .out_11(npc_1_out_11));
  Hex_Digit_Display hex_digit_display_1 (.value(SyscallOut[31:28]));  // open: dp
  Divider divider_1 (.in_1(PC_q), .out_2(divider_1_out_2));
  Hex_Digit_Display hex_digit_display_2 (.value(SyscallOut[23:20]));  // open: dp
  Hex_Digit_Display hex_digit_display_3 (.value(SyscallOut[27:24]));  // open: dp
  Hex_Digit_Display hex_digit_display_4 (.value(SyscallOut[15:12]));  // open: dp
  Hex_Digit_Display hex_digit_display_5 (.value(SyscallOut[19:16]));  // open: dp
  ROM #(.addrWidth(10), .dataWidth(32)) rom_1 (.addr(divider_1_out_2), .data(rom_1_data));  // open: sel
  Hex_Digit_Display hex_digit_display_6 (.value(SyscallOut[11:8]));  // open: dp
  Hex_Digit_Display hex_digit_display_7 (.value(SyscallOut[7:4]));  // open: dp
  Controller controller_1 (
    .in_1(decoder_1_out_3), .in_2(decoder_1_out_7), .out_5(controller_1_out_5), .out_10(controller_1_out_10),
    .out_14(controller_1_out_14), .out_6(controller_1_out_6), .out_11(controller_1_out_11),
    .out_15(controller_1_out_15), .out_7(controller_1_out_7), .out_12(controller_1_out_12),
    .out_13(controller_1_out_13), .out_17(controller_1_out_17), .out_20(controller_1_out_20),
    .out_8(controller_1_out_8), .out_16(controller_1_out_16), .out_21(controller_1_out_21), .in_3(CLK),
    .in_4(RST), .out_9(\有条件分支指令数 ), .out_18(\无条件分支指令数 ), .out_19(controller_1_out_19));
  Decoder decoder_1 (
    .out_2(decoder_1_out_2), .out_3(decoder_1_out_3), .out_4(decoder_1_out_4), .out_5(decoder_1_out_5),
    .in_1(rom_1_data), .out_6(decoder_1_out_6), .out_7(decoder_1_out_7), .out_8(decoder_1_out_8),
    .out_9(decoder_1_out_9));
  Hex_Digit_Display hex_digit_display_8 (.value(SyscallOut[3:0]));  // open: dp
  // Probe on \总周期数 
  // Probe on \无条件分支指令数 
  // Probe on \有条件分支成功跳转 
  Multiplexer #(.select(2), .width(32), .disabled(0), .enable("false")) multiplexer_1 (
    .in0(alu_1_result), .in1(npc_1_out_12), .in2(mips_ram_1_p8), .out(multiplexer_1_out),
    .sel(controller_1_out_17));  // open: in3
  Multiplexer #(.select(2), .width(5), .disabled(0), .enable("false")) multiplexer_2 (
    .in0(decoder_1_out_8), .in1(decoder_1_out_6), .in2({5{1'b1}}), .out(multiplexer_2_out),
    .sel(controller_1_out_13));  // open: in3
  Multiplexer #(.width(5), .disabled(0), .enable("false")) multiplexer_3 (
    .in0(decoder_1_out_4), .in1(5'b00010), .out(multiplexer_3_out), .sel(controller_1_out_7));
  // RegisterFile registerfile_1: pin names not known; wires that end beside it: multiplexer_1_out, CLK, controller_1_out_20, multiplexer_2_out, multiplexer_3_out, registerfile_1_p6, registerfile_1_p7, registerfile_1_p8
  Multiplexer #(.width(5), .disabled(0), .enable("false")) multiplexer_4 (
    .in0(decoder_1_out_6), .in1(5'b00100), .out(registerfile_1_p6), .sel(controller_1_out_12));
  Extender extender_1 (
    .in_1(decoder_1_out_2), .out_3(extender_1_out_3), .out_4(extender_1_out_4), .in_2(decoder_1_out_9));
  Multiplexer #(.width(32), .disabled(0), .enable("false")) multiplexer_5 (
    .in0(registerfile_1_p7), .in1(extender_1_out_3), .out(multiplexer_5_out), .sel(controller_1_out_5));
  Multiplexer #(.width(32), .disabled(0), .enable("false")) multiplexer_6 (
    .in0(registerfile_1_p8), .in1(extender_1_out_4), .out(multiplexer_6_out), .sel(controller_1_out_10));
  Syscall syscall_1 (.in_1(controller_1_out_16), .out_5(SyscallOut), .in_2(CLK), .in_3(RST), .in_4(registerfile_1_p8));
  ALU alu_1 (.AluOP(controller_1_out_14), .X(multiplexer_5_out), .Result(alu_1_result), .Y(multiplexer_6_out));
  Divider1 divider1_1 (.in_1(alu_1_result), .out_2(divider1_1_out_2));
  // MIPS_RAM mips_ram_1: pin names not known; wires that end beside it: divider1_1_out_2, registerfile_1_p8, controller_1_out_11, controller_1_out_6, CLK, controller_1_out_15, RST, mips_ram_1_p8

  // Notes on the sheet:
  //   中断源
  //   中断请求指示
  //   contents of rom_1 (hex, n*v repeats v):
  //   20110001 8000c05 20110001 20120002 20130003 8000c09 20110001 20120002 20130003 8000c0d 20110001
  //   20120002 20130003 8000c11 20110001 20120002 20130003 c000cb8 20100001 20110001 118fc0 112020
  //   20020022 c 118882 12200001 8000c15 112020 20020022 c 20110001 118880 112020 20020022 c 12200001
  //   8000c1f 20110001 118fc0 112020 20020022 c 1188c3 112020 20020022 c 118903 112020 20020022 c 118903
  //   112020 20020022 c 118903 112020 20020022 c 118903 112020 20020022 c 118903 112020 20020022 c 118903
  //   112020 20020022 c 118903 112020 20020022 c 20100001 109fc0 139fc3 8021 2012000c 24160003 26100001
  //   3210000f 20080008 20090001 139900 2709825 132020 20020022 c 1094022 1500fff9 22100001 2018000f
  //   2188024 108700 20080008 20090001 139902 2709825 132021 20020022 c 1094022 1500fff9 108702 2c9b022
  //   12c00001 8000c50 4020 1084027 84400 3508ffff 82021 20020022 c 2010ffff 20110000 ae300000 22100001
  //   22310004 ae300000 22100001 22310004 ae300000 22100001 22310004 ae300000 22100001 22310004 ae300000
  //   22100001 22310004 ae300000 22100001 22310004 ae300000 22100001 22310004 ae300000 22100001 22310004
  //   ae300000 22100001 22310004 ae300000 22100001 22310004 ae300000 22100001 22310004 ae300000 22100001
  //   22310004 ae300000 22100001 22310004 ae300000 22100001 22310004 ae300000 22100001 22310004 ae300000
  //   22100001 22310004 22100001 8020 2011003c 8e130000 8e340000 274402a 11000002 ae330000 ae140000
  //   2231fffc 1611fff8 102020 20020022 c 22100004 2011003c 1611fff2 2002000a c 20100000 22100001 102020
  //   20020022 c 22100002 102020 20020022 c 22100003 102020 20020022 c 22100004 102020 20020022 c 22100005
  //   102020 20020022 c 22100006 102020 20020022 c 22100007 102020 20020022 c 22100008 102020 20020022
  //   20020022 c 3e00008 201d7fff 27bdfffc afb60000 27bdfffc afb40000 27bdfffc afb50000 27bdfffc afb00000
  //   27bdfffc afb30000 27bdfffc afa40000 27bdfffc afa20000 20160001 20140006 20150001 168020 108100
  //   2149825 132020 20020022 c 1600fffa 295a022 1680fff7 8fa20000 27bd0004 8fa40000 27bd0004 8fb30000
  //   27bd0004 8fb00000 27bd0004 8fb50000 27bd0004 8fb40000 27bd0004 8fb60000 27bd0004 42000018 201d7fff
  //   27bdfffc afb60000 27bdfffc afb40000 27bdfffc afb50000 27bdfffc afb00000 27bdfffc afb30000 27bdfffc
  //   afa40000 27bdfffc afa20000 20160002 20140006 20150001 168020 108100 2149825 132020 20020022 c
  //   1600fffa 295a022 1680fff7 8fa20000 27bd0004 8fa40000 27bd0004 8fb30000 27bd0004 8fb00000 27bd0004
  //   8fb50000 27bd0004 8fb40000 27bd0004 8fb60000 27bd0004 42000018 201d7fff 27bdfffc afb60000 27bdfffc
  //   afb40000 27bdfffc afb50000 27bdfffc afb00000 27bdfffc afb30000 27bdfffc afa40000 27bdfffc afa20000
  //   20160003 20140006 20150001 168020 108100 2149825 132020 20020022 c 1600fffa 295a022 1680fff7
  //   8fa20000 27bd0004 8fa40000 27bd0004 8fb30000 27bd0004 8fb00000 27bd0004 8fb50000 27bd0004 8fb40000
  //   27bd0004 8fb60000 27bd0004 42000018
  //   数码管输出
endmodule

module Controller (
  input  [5:0] in_1,
  input  [5:0] in_2,
  input  in_3,
  input  in_4,
  output out_5,
  output [3:0] out_6,
  output out_7,
  output [2:0] out_8,
  output [15:0] out_9,
  output out_10,
  output out_11,
  output out_12,
  output [1:0] out_13,
  output [3:0] out_14,
  output out_15,
  output out_16,
  output [1:0] out_17,
  output [15:0] out_18,
  output out_19,
  output out_20,
  output out_21
);

  wire add, addi, addiu, adds, addu, \and , andi, ands, beq, bltz, bne, cmps, comparator_1_eq,
       comparator_17_eq, comparator_18_eq, comparator_19_eq, comparator_20_eq, comparator_21_eq,
       comparator_22_eq, comparator_23_eq, comparator_24_eq, comparator_25_eq, comparator_26_eq,
       comparator_27_eq, comparator_28_eq, comparator_29_eq, comparator_30_eq, j, jal, jr, js, \nor , \or ,
       or_6_out, or_9_out, or_10_out, or_11_out, ori, ors, rlshifters, sb, sll, slt, slti, sltu, sra, srl,
       srlv, sub, sw, xori;

  Comparator #(.width(6)) comparator_1 (.a(in_1), .b({6{1'b0}}), .eq(comparator_1_eq));  // open: gt, lt
  Comparator #(.width(6)) comparator_2 (.a(in_1), .b(6'b001000), .eq(addi));  // open: gt, lt
  Comparator #(.width(6)) comparator_3 (.a(in_1), .b(6'b001001), .eq(addiu));  // open: gt, lt
  Comparator #(.width(6)) comparator_4 (.a(in_1), .b(6'b001100), .eq(andi));  // open: gt, lt
  Comparator #(.width(6)) comparator_5 (.a(in_1), .b(6'b001101), .eq(ori));  // open: gt, lt
  Comparator #(.width(6)) comparator_6 (.a(in_1), .b(6'b001110), .eq(xori));  // open: gt, lt
  Comparator #(.width(6)) comparator_7 (.a(in_1), .b(6'b001010), .eq(slti));  // open: gt, lt
  Comparator #(.width(6)) comparator_8 (.a(in_1), .b(6'b100011), .eq(out_15));  // open: gt, lt
  Comparator #(.width(6)) comparator_9 (.a(in_1), .b(6'b101011), .eq(sw));  // open: gt, lt
  Comparator #(.width(6)) comparator_10 (.a(in_1), .b(6'b101000), .eq(sb));  // open: gt, lt
  Comparator #(.width(6)) comparator_11 (.a(in_1), .b(6'b000100), .eq(beq));  // open: gt, lt
  Comparator #(.width(6)) comparator_12 (.a(in_1), .b(6'b000101), .eq(bne));  // open: gt, lt
  Comparator #(.width(6)) comparator_13 (.a(in_1), .b(6'b000001), .eq(bltz));  // open: gt, lt
  Comparator #(.width(6)) comparator_14 (.a(in_1), .b(6'b000010), .eq(j));  // open: gt, lt
  Comparator #(.width(6)) comparator_15 (.a(in_1), .b(6'b000011), .eq(jal));  // open: gt, lt
  Comparator #(.width(6)) comparator_16 (.a(in_1), .b(6'b010000), .eq(out_19));  // open: gt, lt
  Comparator #(.width(6)) comparator_17 (.a(in_2), .b(6'b100000), .eq(comparator_17_eq));  // open: gt, lt
  Comparator #(.width(6)) comparator_18 (.a(in_2), .b(6'b100001), .eq(comparator_18_eq));  // open: gt, lt
  Comparator #(.width(6)) comparator_19 (.a(in_2), .b(6'b100100), .eq(comparator_19_eq));  // open: gt, lt
  Comparator #(.width(6)) comparator_20 (.a(in_2), .b(6'b100010), .eq(comparator_20_eq));  // open: gt, lt
  Comparator #(.width(6)) comparator_21 (.a(in_2), .b(6'b100101), .eq(comparator_21_eq));  // open: gt, lt
  Comparator #(.width(6)) comparator_22 (.a(in_2), .b(6'b100111), .eq(comparator_22_eq));  // open: gt, lt
  Comparator #(.width(6)) comparator_23 (.a(in_2), .b(6'b000110), .eq(comparator_23_eq));  // open: gt, lt
  Comparator #(.width(6)) comparator_24 (.a(in_2), .b(6'b101010), .eq(comparator_24_eq));  // open: gt, lt
  Comparator #(.width(6)) comparator_25 (.a(in_2), .b(6'b101011), .eq(comparator_25_eq));  // open: gt, lt
  Comparator #(.width(6)) comparator_26 (.a(in_2), .b({6{1'b0}}), .eq(comparator_26_eq));  // open: gt, lt
  Comparator #(.width(6)) comparator_27 (.a(in_2), .b(6'b000011), .eq(comparator_27_eq));  // open: gt, lt
  Comparator #(.width(6)) comparator_28 (.a(in_2), .b(6'b000010), .eq(comparator_28_eq));  // open: gt, lt
  Comparator #(.width(6)) comparator_29 (.a(in_2), .b(6'b001000), .eq(comparator_29_eq));  // open: gt, lt
  Comparator #(.width(6)) comparator_30 (.a(in_2), .b(6'b001100), .eq(comparator_30_eq));  // open: gt, lt
  and and_1 (add, comparator_1_eq, comparator_17_eq);
  and and_2 (addu, comparator_1_eq, comparator_18_eq);
  and and_3 (\and , comparator_1_eq, comparator_19_eq);
  and and_4 (sub, comparator_1_eq, comparator_20_eq);
  and and_5 (\or , comparator_1_eq, comparator_21_eq);
  and and_6 (\nor , comparator_1_eq, comparator_22_eq);
  and and_7 (srlv, comparator_1_eq, comparator_23_eq);
  and and_8 (slt, comparator_1_eq, comparator_24_eq);
  and and_9 (sltu, comparator_1_eq, comparator_25_eq);
  and and_10 (sll, comparator_1_eq, comparator_26_eq);
  and and_11 (sra, comparator_1_eq, comparator_27_eq);
  and and_12 (srl, comparator_1_eq, comparator_28_eq);
  and and_13 (jr, comparator_1_eq, comparator_29_eq);
  and and_14 (out_16, comparator_1_eq, comparator_30_eq);
  or or_1 (cmps, slti, bltz, slt);
  or or_2 (ors, \or , ori);
  or or_3 (ands, \and , andi);
  or or_4 (rlshifters, srlv, srl);
  or or_5 (out_5, sll, sra, srl);
  or or_6 (or_6_out, addi, addiu, andi, ori, xori, slti, out_15, sw, sb);
  or or_7 (adds, out_15, add, addi, sb, addu, addiu, sw);
  Priority_Encoder #(.select(4)) priority_encoder_1 (
    .in0(1'b1), .in1(sra), .in2(rlshifters), .in3(1'b0), .in4(1'b0), .in5(adds), .in6(sub), .in7(ands),
    .in8(ors), .in9(xori), .in10(\nor ), .in11(cmps), .in12(sltu), .in13(1'b0), .in14(1'b0), .in15(1'b0),
    .out(out_14));  // open: gs, en_out, en_in
  Priority_Encoder #(.select(1)) priority_encoder_2 (
    .in0(1'b1), .in1(or_6_out), .out(out_10));  // open: gs, en_out, en_in
  not not_1 (out_6[3], sb);
  or or_8 (out_11, sw, sb);
  Priority_Encoder #(.select(1)) priority_encoder_3 (.in0(1'b1), .in1(out_16), .out(out_7));  // open: gs, en_out, en_in
  or or_9 (or_9_out, addi, addiu, andi, ori, xori, slti, out_15);
  Priority_Encoder #(.select(2)) priority_encoder_4 (
    .in0(1'b1), .in1(jal), .in2(out_15), .in3(1'b0), .out(out_17));  // open: gs, en_out, en_in
  nor nor_1 (out_20, sw, sb, beq, bne, bltz, j, jr, out_16);
  Priority_Encoder #(.select(2)) priority_encoder_5 (
    .in0(1'b1), .in1(or_9_out), .in2(jal), .in3(1'b0), .out(out_13));  // open: gs, en_out, en_in
  or or_10 (or_10_out, bltz, bne, beq);
  or or_11 (or_11_out, j, jal, jr);
  or or_12 (js, j, jal);
  Priority_Encoder priority_encoder_6 (
    .in0(1'b1), .in1(beq), .in2(bne), .in3(bltz), .in4(js), .in5(jr), .in6(1'b0), .in7(1'b0), .out(out_8));  // open: en_in, gs, en_out
  not not_2 (out_21, out_16);
  Counter #(.width(16), .max('hffff)) counter_1 (
    .count(or_10_out), .Q(out_9), .clk(in_3), .clr(in_4));  // open: load, D, carry
  Counter #(.width(16), .max('hffff)) counter_2 (
    .count(or_11_out), .Q(out_18), .clk(in_3), .clr(in_4));  // open: load, D, carry

  assign out_6[2:0] = {{2{out_6[3]}}, 1'b1};
  assign out_12 = out_7;

  // Other names for the same wires on the sheet: ALUop[3:0] = out_14; CA = out_5; CB = out_10; CLK = in_3;
  //   CPC[2:0] = out_8; Din[1:0] = out_17; eret = out_19; funct[5:0] = in_2; ld = out_15; lw = out_15; op[5:0] = in_1;
  //   Ra = out_7; Rb = out_7; RST = in_4; Rw[1:0] = out_13; Sel[3:1] = {3{out_6[3]}}; str = out_11; SysC2 = out_21;
  //   SysC1 = out_16; syscall = out_16; We = out_20; 无条件[15:0] = out_18; 有条件[15:0] = out_9
endmodule

module NPC (
  input  [15:0] in_1,
  input  [31:0] in_2,
  input  in_3,
  input  [31:0] in_4,
  input  [2:0] in_5,
  input  in_6,
  input  in_7,
  input  [25:0] in_8,
  input  [31:0] in_9,
  output [31:0] out_10,
  output out_11,
  output [31:0] out_12,
  output [15:0] out_13
);

  wire and_2_out, and_3_out, and_4_out, comparator_1_eq, comparator_2_eq, comparator_3_lt, comparator_4_eq,
       comparator_5_eq, comparator_6_eq, not_1_out, not_2_out, or_3_out;
  wire [31:0] and_1_out, bit_extender_1_out, bit_extender_2_out, Cbeq, Cbltz, Cbne, PC4offset, PCLabel;

  Adder #(.width(32)) adder_1 (.a(in_2), .b(32'h4), .out(out_12));  // open: cin, cout
  Comparator #(.width(32)) comparator_1 (.a(in_4), .b(32'ha), .eq(comparator_1_eq));  // open: gt, lt
  assign bit_extender_1_out = {{14{in_1[15]}}, {in_1, 2'b00}};  // Bit_Extender bit_extender_1
  assign and_1_out = in_2 & 32'hf0000000;  // AND_Gate and_1, 32 bits wide
  assign bit_extender_2_out = {{4{1'b0}}, {in_8, 2'b00}};  // Bit_Extender bit_extender_2
  not not_1 (not_1_out, comparator_1_eq);
  Adder #(.width(32)) adder_2 (.a(bit_extender_1_out), .b(out_12), .out(PC4offset));  // open: cin, cout
  assign PCLabel = and_1_out | bit_extender_2_out;  // OR_Gate or_1, 32 bits wide
  or or_2 (out_11, not_1_out, in_3);
  Comparator #(.width(32)) comparator_2 (.a(in_4), .b(in_9), .eq(comparator_2_eq));  // open: gt, lt
  Comparator #(.width(32)) comparator_3 (.a(in_4), .b(in_9), .lt(comparator_3_lt));  // open: gt, eq
  Multiplexer #(.width(32), .disabled(0), .enable("false")) multiplexer_1 (
    .in0(out_12), .in1(PC4offset), .out(Cbeq), .sel(comparator_2_eq));
  Multiplexer #(.width(32), .disabled(0), .enable("false")) multiplexer_2 (
    .in0(PC4offset), .in1(out_12), .out(Cbne), .sel(comparator_2_eq));
  Comparator #(.width(3)) comparator_4 (.a(in_5), .b(3'b001), .eq(comparator_4_eq));  // open: gt, lt
  Comparator #(.width(3)) comparator_5 (.a(in_5), .b(3'b010), .eq(comparator_5_eq));  // open: gt, lt
  not not_2 (not_2_out, comparator_2_eq);
  Comparator #(.width(3)) comparator_6 (.a(in_5), .b(3'b011), .eq(comparator_6_eq));  // open: gt, lt
  Multiplexer #(.width(32), .disabled(0), .enable("false")) multiplexer_3 (
    .in0(out_12), .in1(PC4offset), .out(Cbltz), .sel(comparator_3_lt));
  and and_2 (and_2_out, comparator_4_eq, comparator_2_eq);
  and and_3 (and_3_out, comparator_5_eq, not_2_out);
  and and_4 (and_4_out, comparator_6_eq, comparator_3_lt);
  Counter #(.width(16), .max('hffff)) counter_1 (
    .count(or_3_out), .Q(out_13), .clk(in_6), .clr(in_7));  // open: load, D, carry
  or or_3 (or_3_out, and_2_out, and_3_out, and_4_out);
  Multiplexer #(.select(3), .width(32), .disabled(0), .enable("false")) multiplexer_4 (
    .in0(out_12), .in1(Cbeq), .in2(Cbne), .in3(Cbltz), .in4(PCLabel), .in5(in_4), .in6({32{1'b0}}),
    .in7({32{1'b0}}), .out(out_10), .sel(in_5));

  // Other names for the same wires on the sheet: IMM[15:0] = in_1; label[25:0] = in_8; CLK = in_6; CNPC[2:0] = in_5;
  //   en = out_11; Input[31:0] = in_2; Output[31:0] = out_10; PC4[31:0] = out_12; RF1[31:0] = in_4; RF2[31:0] = in_9;
  //   RST = in_7; success[15:0] = out_13; syscall = in_3
endmodule

module Divider (
  input  [31:0] in_1,
  output [9:0] out_2
);


  assign out_2 = in_1[11:2];

  // Other names for the same wires on the sheet: Input[31:0] = in_1; Output[9:0] = in_1[11:2]
endmodule

module Divider1 (
  input  [31:0] in_1,
  output [23:0] out_2
);


  assign out_2 = in_1[25:2];

  // Other names for the same wires on the sheet: Input[31:0] = in_1; Output[23:0] = in_1[25:2]
endmodule

module Decoder (
  input  [31:0] in_1,
  output [4:0] out_2,
  output [5:0] out_3,
  output [4:0] out_4,
  output [25:0] out_5,
  output [4:0] out_6,
  output [5:0] out_7,
  output [4:0] out_8,
  output [15:0] out_9
);


  assign out_2 = in_1[10:6];
  assign out_3 = in_1[31:26];
  assign out_4 = in_1[25:21];
  assign out_5 = in_1[25:0];
  assign out_6 = in_1[20:16];
  assign out_7 = in_1[5:0];
  assign out_8 = in_1[15:11];
  assign out_9 = in_1[15:0];

  // Other names for the same wires on the sheet: funct[5:0] = in_1[5:0]; IMM[15:0] = in_1[15:0]; Input[31:0] = in_1;
  //   label[25:0] = in_1[25:0]; s[4:0] = in_1[10:6]; rd[4:0] = in_1[15:11]; rt[4:0] = in_1[20:16];
  //   rs[4:0] = in_1[25:21]; op[5:0] = in_1[31:26]
endmodule

module Extender (
  input  [4:0] in_1,
  input  [15:0] in_2,
  output [31:0] out_3,
  output [31:0] out_4
);

  assign out_3 = {{27{in_1[4]}}, in_1};  // Bit_Extender bit_extender_1
  assign out_4 = {{16{in_2[15]}}, in_2};  // Bit_Extender bit_extender_2

  // Other names for the same wires on the sheet: eIMM[31:0] = out_4; es[31:0] = out_3; IMM[15:0] = in_2;
  //   s[4:0] = in_1
endmodule

module SumPeriod (
  input  in_1,
  input  in_2,
  input  in_3,
  output [15:0] out_4
);

  wire [15:0] adder_1_out, counter_1_q;

  Counter #(.width(16), .max('hffff)) counter_1 (
    .count(in_1), .Q(counter_1_q), .clk(in_2), .clr(in_3));  // open: load, D, carry
  Adder #(.width(16)) adder_1 (.a(16'h1), .b(counter_1_q), .out(adder_1_out));  // open: cin, cout
  Multiplexer #(.width(16), .disabled(0), .enable("false")) multiplexer_1 (
    .in0(adder_1_out), .in1(counter_1_q), .out(out_4), .sel(in_1));

  // Other names for the same wires on the sheet: CLK = in_2; cnt[15:0] = out_4; enable = in_1; RST = in_3
endmodule

module Syscall (
  input  in_1,
  input  in_2,
  input  in_3,
  input  [31:0] in_4,
  output [31:0] out_5
);

  Register #(.width(32)) register_1 (.D(in_4), .en(in_1), .Q(out_5), .clk(in_2), .clr(in_3));

  // Other names for the same wires on the sheet: CLK = in_2; enable = in_1; Input[31:0] = in_4; Output[31:0] = out_5;
  //   RST = in_3
endmodule

module interrupt (
  input  intr_btn1,
  input  intr_btn2,
  input  intr_btn3,
  input  eret,
  input  [31:0] PC,
  output intr_LED1,
  output [31:0] PC_out,
  output intr_LED2,
  output intr_LED3
);

  wire and_1_out, and_2_out, and_3_out, clk, d_ff_1_q, d_ff_2_q, d_ff_3_q, d_ff_7_q, decoder_1_out1,
       decoder_1_out2, decoder_1_out3, hasIntr, intr1, intr2, intr3, intr_en, nand_1_out, nand_2_out,
       nand_3_out, not_1_out, or_4_out, or_5_out, or_6_out, or_7_out;
  wire [1:0] choose, current;
  wire [31:0] multiplexer_2_out, savePC, vector;

  Clock clock_1 (.out(clk));
  Decoder_part #(.select(2), .disabled(0), .enable("false")) decoder_1 (
    .out1(decoder_1_out1), .out2(decoder_1_out2), .out3(decoder_1_out3), .sel(current));  // open: out0
  nand nand_1 (nand_1_out, eret, decoder_1_out1);
  nand nand_2 (nand_2_out, eret, decoder_1_out2);
  nand nand_3 (nand_3_out, eret, decoder_1_out3);
  Priority_Encoder #(.select(2), .disabled(0)) priority_encoder_1 (
    .in0(1'b1), .in1(intr1), .in2(intr2), .in3(intr3), .out(choose), .en_in(intr_en));  // open: gs, en_out
  Register #(.width(2)) register_1 (.D(choose), .en(hasIntr), .Q(current), .clk(clk));  // open: clr
  D_Flip_Flop d_ff_1 (.clk(intr_btn1), .D(1'b1), .Q(d_ff_1_q), .reset(intr1));  // open: Qn, preset, en
  or or_1 (intr_LED1, intr1, d_ff_1_q);
  D_Flip_Flop d_ff_2 (.clk(intr_btn2), .D(1'b1), .Q(d_ff_2_q), .reset(intr2));  // open: Qn, preset, en
  or or_2 (intr_LED2, intr2, d_ff_2_q);
  D_Flip_Flop d_ff_3 (.clk(intr_btn3), .D(1'b1), .Q(d_ff_3_q), .reset(intr3));  // open: Qn, preset, en
  or or_3 (intr_LED3, intr3, d_ff_3_q);
  or or_4 (or_4_out, d_ff_1_q, intr1);
  or or_5 (or_5_out, d_ff_2_q, intr2);
  or or_6 (or_6_out, d_ff_3_q, intr3);
  and and_1 (and_1_out, or_4_out, nand_1_out);
  and and_2 (and_2_out, or_5_out, nand_2_out);
  and and_3 (and_3_out, or_6_out, nand_3_out);
  D_Flip_Flop d_ff_4 (.clk(clk), .D(and_1_out), .Q(intr1));  // open: Qn, preset, en, reset
  D_Flip_Flop d_ff_5 (.clk(clk), .D(and_2_out), .Q(intr2));  // open: Qn, preset, en, reset
  D_Flip_Flop d_ff_6 (.clk(clk), .D(and_3_out), .Q(intr3));  // open: Qn, preset, en, reset
  Multiplexer #(.select(2), .width(32), .disabled(0), .enable("false")) multiplexer_1 (
    .in0({32{1'b0}}), .in1(32'h336c), .in2(32'h3414), .in3(32'h34bc), .out(vector), .sel(choose));
  or or_7 (or_7_out, intr1, intr2, intr3);
  and and_4 (hasIntr, or_7_out, intr_en);
  Register #(.width(32)) register_2 (.D(PC), .en(hasIntr), .Q(savePC), .clk(clk));  // open: clr
  not not_1 (not_1_out, d_ff_7_q);
  D_Flip_Flop d_ff_7 (.clk(clk), .D(1'b1), .Q(d_ff_7_q), .en(hasIntr), .reset(eret));  // open: Qn, preset
  Multiplexer #(.width(32), .disabled(0), .enable("false")) multiplexer_2 (
    .in0(PC), .in1(vector), .out(multiplexer_2_out), .sel(hasIntr));
  D_Flip_Flop #(.trigger("falling")) d_ff_8 (.clk(clk), .D(not_1_out), .Q(intr_en));  // open: Qn, preset, en, reset
  Multiplexer #(.width(32), .disabled(0), .enable("false")) multiplexer_3 (
    .in0(multiplexer_2_out), .in1(savePC), .out(PC_out), .sel(eret));
endmodule
